// Logisim project PROCESSADOR.circ as structural Verilog: 7 circuits, main circuit main
// OP
module main (
  output [31:0] out_1,
  output [31:0] out_2,
  output [31:0] out_3
);

  wire and_1_out, and_2_out, clock_1_out, comparator_1_eq, or_1_out, RESET_out, uc_1_beq, uc_1_jump,
       uc_1_load_mem, uc_1_reg_write, uc_1_write_mem;
  wire [1:0] uc_1_ula_op;
  wire [2:0] OPCODE;
  wire [4:0] RD, RT, RW;
  wire [7:0] adder_1_out, ADDRESS, conversor_32_8_1_saida, multiplexer_1_out, register_1_q;
  wire [15:0] IMMEDIATE;
  wire [31:0] multiplexer_2_out, ram_1_data, \ula_1_saída ;

  SEPARADOR_DE_INSTRUCAO separador_de_instrucao_1 (
    .INSTRUCAO(out_3), .IMMEDIATE(IMMEDIATE), .ADDRESS(ADDRESS), .OPCODE(OPCODE), .RW(RW), .RT(RT), .RD(RD));
  Adder adder_1 (.a(register_1_q), .b(8'h1), .out(adder_1_out));  // open: cin, cout
  and and_1 (and_1_out, ~uc_1_beq, uc_1_jump);  // AND_Gate
  Multiplexer #(.width(8), .enable("false")) multiplexer_1 (
    .in0(adder_1_out), .in1(ADDRESS), .out(multiplexer_1_out), .sel(or_1_out));
  or or_1 (or_1_out, and_1_out, and_2_out);
  and and_2 (and_2_out, uc_1_beq, comparator_1_eq);
  Register register_1 (.D(multiplexer_1_out), .en(1'b1), .Q(register_1_q), .clk(clock_1_out), .clr(RESET_out));
  Clock clock_1 (.out(clock_1_out));
  Button RESET (.out(RESET_out));
  ROM #(.dataWidth(32)) rom_1 (.addr(register_1_q), .data(out_3));  // open: sel
  Multiplexer #(.width(32), .enable("false")) multiplexer_2 (
    .in0(\ula_1_saída ), .in1(ram_1_data), .out(multiplexer_2_out), .sel(uc_1_load_mem));
  UC uc_1 (
    .in_1(OPCODE), .ULA_OP(uc_1_ula_op), .REG_WRITE(uc_1_reg_write), .WRITE_MEM(uc_1_write_mem),
    .LOAD_MEM(uc_1_load_mem), .JUMP(uc_1_jump), .BEQ(uc_1_beq));
  Banco_de_Registradores banco_de_registradores_1 (
    .INPUT_VALUE(multiplexer_2_out), .RT_OUT(out_1), .RS_OUT(out_2), .RD(RD), .RS(RW), .RT(RT),
    .RESET(RESET_out), .REG_WRITE(uc_1_reg_write));
  ULA ula_1 (.RT(out_1), .RS(out_2), .\SAÍDA (\ula_1_saída ), .OP_CODE(uc_1_ula_op), .IMMEDIATE(IMMEDIATE));
  Comparator #(.width(32)) comparator_1 (.a(out_2), .b(out_1), .eq(comparator_1_eq));  // open: gt, lt
  CONVERSOR_32__8 conversor_32_8_1 (.INPUT(out_2), .SAIDA(conversor_32_8_1_saida));
  RAM #(.dataWidth(32), .bus("separate")) ram_1 (
    .addr(conversor_32_8_1_saida), .din(out_1), .data(ram_1_data), .clk(uc_1_write_mem));  // open: str, sel, ld, clr

  // Other names for the same wires on the sheet: INST[31:0] = out_3

  // Notes on the sheet:
  //   contents of rom_1 (hex, n*v repeats v):
  //   41000000 42000200 43000400 44000020 45000000 85210000 46000000 8620f000 48000000 47000000 8720c000
  //   29290000 949c000 9484000 c9480000 2a390000 a518000 a508000 ca500000 294a8000 8424000 47380008
  //   60005800 29290000 9498000 948c000 a8480000 46300008 60004000 45280008 60003000
  //   DATA MEMORY
endmodule

// BR
module Banco_de_Registradores (
  input  [31:0] INPUT_VALUE,
  input  [4:0] RT,
  input  [4:0] RD,
  input  [4:0] RS,
  input  RESET,
  input  REG_WRITE,
  output [31:0] RT_OUT,
  output [31:0] RS_OUT
);

  wire _1, _2, _3, _4, _5, _6, _7, _8, _9, _10, _11, _12, _13, _14, _15, _16, _17, _18, _19, _20, _21, _22,
       _23, _24, _25, _26, _27, _28, _29, _30, _31, and_1_out, and_2_out, and_3_out, and_4_out, and_5_out,
       and_6_out, and_7_out, and_8_out, and_9_out, and_10_out, and_11_out, and_12_out, and_13_out,
       and_14_out, and_15_out, and_16_out, and_17_out, and_18_out, and_19_out, and_20_out, and_21_out,
       and_22_out, and_23_out, and_24_out, and_25_out, and_26_out, and_27_out, and_28_out, and_29_out,
       and_30_out, and_31_out;
  wire [31:0] S0, S1, S2, S3, S4, S5, S6, S7, S8, S9, S10, S11, S12, S13, S14, S15, S16, S17, S18, S19, S20,
       S21, S22, S23, S24, S25, S26, S27, S28, S29, S30, S31, S230;

  Demultiplexer #(.select(5), .enable("false")) demultiplexer_1 (
    .out1(_1), .out2(_2), .out3(_3), .out4(_4), .out5(_5), .out6(_6), .out7(_7), .out8(_8), .out9(_9),
    .out10(_10), .out11(_11), .out12(_12), .out13(_13), .out14(_14), .out15(_15), .out16(_16), .out17(_17),
    .out18(_18), .out19(_19), .out20(_20), .out21(_21), .out22(_22), .out23(_23), .out24(_24), .out25(_25),
    .out26(_26), .out27(_27), .out28(_28), .out29(_29), .out30(_30), .out31(_31), .in(1'b1), .sel(RD));  // open: out0
  Register #(.width(32)) R0 (.Q(S0));  // open: D, en, clk, clr
  Register #(.width(32)) R8 (.D(INPUT_VALUE), .Q(S8), .clk(and_1_out), .clr(RESET));  // open: en
  and and_1 (and_1_out, _8, REG_WRITE);
  Register #(.width(32)) R16 (.D(INPUT_VALUE), .Q(S16), .clk(and_2_out), .clr(RESET));  // open: en
  and and_2 (and_2_out, _16, REG_WRITE);
  Register #(.width(32)) R24 (.D(INPUT_VALUE), .Q(S24), .clk(and_3_out), .clr(RESET));  // open: en
  and and_3 (and_3_out, _24, REG_WRITE);
  and and_4 (and_4_out, _1, REG_WRITE);
  and and_5 (and_5_out, _9, REG_WRITE);
  and and_6 (and_6_out, _17, REG_WRITE);
  and and_7 (and_7_out, _25, REG_WRITE);
  Register #(.width(32)) R1 (.D(INPUT_VALUE), .Q(S1), .clk(and_4_out), .clr(RESET));  // open: en
  and and_8 (and_8_out, _2, REG_WRITE);
  Register #(.width(32)) R9 (.D(INPUT_VALUE), .Q(S9), .clk(and_5_out), .clr(RESET));  // open: en
  and and_9 (and_9_out, _10, REG_WRITE);
  Register #(.width(32)) R17 (.D(INPUT_VALUE), .Q(S17), .clk(and_6_out), .clr(RESET));  // open: en
  and and_10 (and_10_out, _18, REG_WRITE);
  Register #(.width(32)) R25 (.D(INPUT_VALUE), .Q(S25), .clk(and_7_out), .clr(RESET));  // open: en
  and and_11 (and_11_out, _26, REG_WRITE);
  Register #(.width(32)) R2 (.D(INPUT_VALUE), .Q(S2), .clk(and_8_out), .clr(RESET));  // open: en
  Register #(.width(32)) R10 (.D(INPUT_VALUE), .Q(S10), .clk(and_9_out), .clr(RESET));  // open: en
  Register #(.width(32)) R18 (.D(INPUT_VALUE), .Q(S18), .clk(and_10_out), .clr(RESET));  // open: en
  Register #(.width(32)) R26 (.D(INPUT_VALUE), .Q(S26), .clk(and_11_out), .clr(RESET));  // open: en
  Register #(.width(32)) R3 (.D(INPUT_VALUE), .Q(S3), .clk(and_12_out), .clr(RESET));  // open: en
  and and_12 (and_12_out, _3, REG_WRITE);
  Register #(.width(32)) R11 (.D(INPUT_VALUE), .Q(S11), .clk(and_13_out), .clr(RESET));  // open: en
  and and_13 (and_13_out, _11, REG_WRITE);
  Register #(.width(32)) R19 (.D(INPUT_VALUE), .Q(S19), .clk(and_14_out), .clr(RESET));  // open: en
  and and_14 (and_14_out, _19, REG_WRITE);
  Register #(.width(32)) R27 (.D(INPUT_VALUE), .Q(S27), .clk(and_15_out), .clr(RESET));  // open: en
  and and_15 (and_15_out, _27, REG_WRITE);
  Register #(.width(32)) R4 (.D(INPUT_VALUE), .Q(S4), .clk(and_16_out), .clr(RESET));  // open: en
  and and_16 (and_16_out, _4, REG_WRITE);
  Register #(.width(32)) R12 (.D(INPUT_VALUE), .Q(S12), .clk(and_17_out), .clr(RESET));  // open: en
  and and_17 (and_17_out, _12, REG_WRITE);
  Register #(.width(32)) R20 (.D(INPUT_VALUE), .Q(S20), .clk(and_18_out), .clr(RESET));  // open: en
  and and_18 (and_18_out, _20, REG_WRITE);
  Register #(.width(32)) R28 (.D(INPUT_VALUE), .Q(S28), .clk(and_19_out), .clr(RESET));  // open: en
  and and_19 (and_19_out, _28, REG_WRITE);
  Register #(.width(32)) R5 (.D(INPUT_VALUE), .Q(S5), .clk(and_20_out), .clr(RESET));  // open: en
  and and_20 (and_20_out, _5, REG_WRITE);
  Register #(.width(32)) R13 (.D(INPUT_VALUE), .Q(S13), .clk(and_21_out), .clr(RESET));  // open: en
  and and_21 (and_21_out, _13, REG_WRITE);
  Register #(.width(32)) R21 (.D(INPUT_VALUE), .Q(S21), .clk(and_22_out), .clr(RESET));  // open: en
  and and_22 (and_22_out, _21, REG_WRITE);
  Register #(.width(32)) R29 (.D(INPUT_VALUE), .Q(S29), .clk(and_23_out), .clr(RESET));  // open: en
  and and_23 (and_23_out, _29, REG_WRITE);
  Register #(.width(32)) R6 (.D(INPUT_VALUE), .Q(S6), .clk(and_24_out), .clr(RESET));  // open: en
  and and_24 (and_24_out, _6, REG_WRITE);
  Register #(.width(32)) R14 (.D(INPUT_VALUE), .Q(S14), .clk(and_25_out), .clr(RESET));  // open: en
  and and_25 (and_25_out, _14, REG_WRITE);
  Register #(.width(32)) R22 (.D(INPUT_VALUE), .Q(S22), .clk(and_26_out), .clr(RESET));  // open: en
  and and_26 (and_26_out, _22, REG_WRITE);
  Register #(.width(32)) R30 (.D(INPUT_VALUE), .Q(S230), .clk(and_27_out), .clr(RESET));  // open: en
  and and_27 (and_27_out, _30, REG_WRITE);
  Register #(.width(32)) R7 (.D(INPUT_VALUE), .Q(S7), .clk(and_28_out), .clr(RESET));  // open: en
  and and_28 (and_28_out, _7, REG_WRITE);
  Register #(.width(32)) R15 (.D(INPUT_VALUE), .Q(S15), .clk(and_29_out), .clr(RESET));  // open: en
  and and_29 (and_29_out, _15, REG_WRITE);
  Register #(.width(32)) R23 (.D(INPUT_VALUE), .Q(S23), .clk(and_30_out), .clr(RESET));  // open: en
  and and_30 (and_30_out, _23, REG_WRITE);
  Register #(.width(32)) R31 (.D(INPUT_VALUE), .Q(S31), .clk(and_31_out), .clr(RESET));  // open: en
  and and_31 (and_31_out, _31, REG_WRITE);
  Multiplexer #(.select(5), .width(32), .enable("false")) multiplexer_1 (
    .in0(S0), .in1(S1), .in2(S2), .in3(S3), .in4(S4), .in5(S5), .in6(S6), .in7(S7), .in8(S8), .in9(S9),
    .in10(S10), .in11(S11), .in12(S12), .in13(S13), .in14(S14), .in15(S15), .in16(S16), .in17(S17),
    .in18(S18), .in19(S19), .in20(S20), .in21(S21), .in22(S22), .in23(S23), .in24(S24), .in25(S25),
    .in26(S26), .in27(S27), .in28(S28), .in29(S29), .in30(S30), .in31(S31), .out(RT_OUT), .sel(RT));
  Multiplexer #(.select(5), .width(32), .enable("false")) multiplexer_2 (
    .in0(S0), .in1(S1), .in2(S2), .in3(S3), .in4(S4), .in5(S5), .in6(S6), .in7(S7), .in8(S8), .in9(S9),
    .in10(S10), .in11(S11), .in12(S12), .in13(S13), .in14(S14), .in15(S15), .in16(S16), .in17(S17),
    .in18(S18), .in19(S19), .in20(S20), .in21(S21), .in22(S22), .in23(S23), .in24(S24), .in25(S25),
    .in26(S26), .in27(S27), .in28(S28), .in29(S29), .in30(S30), .in31(S31), .out(RS_OUT), .sel(RS));

  // Other names for the same wires on the sheet: CLK = REG_WRITE
endmodule

module ULA (
  input  [31:0] RT,
  input  [31:0] RS,
  input  [15:0] IMMEDIATE,
  input  [1:0] OP_CODE,
  output [31:0] \SAÍDA 
);

  wire [31:0] adder_1_out, adder_2_out, conversor_16_32_1_saida, multiplier_1_out;

  CONVERSOR_16____32 conversor_16_32_1 (.INPUT(IMMEDIATE), .SAIDA(conversor_16_32_1_saida));
  Adder #(.width(32)) adder_1 (.a(RT), .b(RS), .out(adder_1_out));  // open: cin, cout
  Multiplier #(.width(32)) multiplier_1 (.a(RT), .b(RS), .out(multiplier_1_out));  // open: cin, cout
  Adder #(.width(32)) adder_2 (.a(RT), .b(conversor_16_32_1_saida), .out(adder_2_out));  // open: cin, cout
  Multiplexer #(.select(2), .width(32), .enable("false")) multiplexer_1 (
    .in0(adder_1_out), .in1(multiplier_1_out), .in2(adder_2_out), .out(\SAÍDA ), .sel(OP_CODE));  // open: in3
endmodule

// CONV
module CONVERSOR_16____32 (
  input  [15:0] INPUT,
  output [31:0] SAIDA
);


  assign SAIDA = {{16{1'b0}}, INPUT};
endmodule

module UC (
  input  [2:0] in_1,
  output [1:0] ULA_OP,
  output REG_WRITE,
  output WRITE_MEM,
  output LOAD_MEM,
  output JUMP,
  output BEQ
);

  wire and_1_out, and_2_out, and_5_out, and_6_out, not_1_out, not_2_out, not_3_out, not_4_out, not_5_out,
       not_6_out, not_7_out, not_8_out, not_9_out, not_10_out;

  not not_1 (not_1_out, in_1[2]);
  not not_2 (not_2_out, in_1[1]);
  not not_3 (not_3_out, in_1[0]);
  not not_4 (not_4_out, in_1[1]);
  not not_5 (not_5_out, in_1[0]);
  not not_6 (not_6_out, in_1[2]);
  not not_7 (not_7_out, in_1[1]);
  not not_8 (not_8_out, in_1[0]);
  not not_9 (not_9_out, in_1[1]);
  not not_10 (not_10_out, in_1[0]);
  and and_1 (and_1_out, not_1_out, not_2_out);
  and and_2 (and_2_out, in_1[1], not_3_out);
  and and_3 (WRITE_MEM, in_1[2], not_4_out, in_1[0]);
  and and_4 (LOAD_MEM, in_1[2], in_1[1], not_5_out);
  and and_5 (and_5_out, not_6_out, in_1[1], in_1[0]);
  and and_6 (and_6_out, in_1[2], not_7_out, not_8_out);
  and and_7 (BEQ, in_1[2], not_9_out, not_10_out);
  or or_1 (REG_WRITE, and_1_out, and_2_out);
  or or_2 (JUMP, and_5_out, and_6_out);

  assign ULA_OP = in_1[1:0];
endmodule

module CONVERSOR_32__8 (
  input  [31:0] INPUT,
  output [7:0] SAIDA
);


  assign SAIDA = INPUT[7:0];
endmodule

module SEPARADOR_DE_INSTRUCAO (
  input  [31:0] INSTRUCAO,
  output [15:0] IMMEDIATE,
  output [7:0] ADDRESS,
  output [2:0] OPCODE,
  output [4:0] RW,
  output [4:0] RT,
  output [4:0] RD
);


  assign ADDRESS = INSTRUCAO[18:11];
  assign IMMEDIATE = INSTRUCAO[18:3];
  assign OPCODE = INSTRUCAO[31:29];
  assign RD = INSTRUCAO[28:24];
  assign RT = INSTRUCAO[23:19];
  assign RW = INSTRUCAO[18:14];
endmodule
